// Digital circuit ALU.dig as structural Verilog
module ALU (
  input  [15:0] B,
  input  [15:0] A,
  input  CIN,
  input  CLK,
  input  INIT,
  input  [3:0] S,
  output [15:0] YH,
  output [15:0] YL,
  output WRK
);

  wire div_sel_1_y, SUB_SEL, WRK_t;
  wire [0:0] FA_H;
  wire [15:0] AND, BSL_H, BSL_L, DIV_H, DIV_L, FA_L, MUL_H, MUL_L, NOT, not__neg_1_y, OR, SEQ, SLT, XOR;

  and and_1 (SUB_SEL, ~S[3], ~S[2], ~S[1], S[0]);  // And
  NOT__NEG not__neg_1 (.A(A), .PASS(SUB_SEL), .NOT__NEG(SUB_SEL), .Y(not__neg_1_y));  // open: CRY
  assign AND = B & A;  // And and_2, 16 bits wide
  assign OR = B | A;  // Or or_1, 16 bits wide
  assign XOR = B ^ A;  // XOr xor_1, 16 bits wide
  assign NOT = ~B;  // Not not_1, 16 bits wide
  SLT_16 slt_16_1 (.A(B), .B(A), .LT(SLT), .EQ(SEQ));
  DIV_16 div_16_1 (.B(B), .D(A), .CLK(CLK), .INIT(INIT), .R(DIV_H), .Q(DIV_L), .W(WRK_t));
  BS_15C bs_15c_1 (.A(B), .S(A[3:0]), .R__L(S[0]), .Y(BSL_L), .CRY(BSL_H));
  FA_16 fa_16_1 (.A(not__neg_1_y), .B(B), .CIN(CIN), .SUM(FA_L), .CRY(FA_H[0]));
  MUL_16 mul_16_1 (.A(A), .B(B), .CH(MUL_H), .CL(MUL_L));
  DIV_SEL div_sel_1 (.S({4'b0000, S}), .Y(div_sel_1_y));
  and and_3 (WRK, WRK_t, div_sel_1_y);
  MUX_16x16 mux_16x16_1 (
    .I0({{15{1'b0}}, FA_H[0]}), .I1({{15{1'b0}}, FA_H[0]}), .I2(MUL_H), .I3(DIV_H), .I4(BSL_H), .I5(BSL_H),
    .I6({16{1'b0}}), .I7({16{1'b0}}), .I8({16{1'b0}}), .I9({16{1'b0}}), .I10({16{1'b0}}), .I11({16{1'b0}}),
    .I12({16{1'b0}}), .I13({16{1'b0}}), .I14({16{1'b0}}), .I15({16{1'b0}}), .S(S), .Y(YH));
  MUX_16x16 mux_16x16_2 (
    .I0(FA_L), .I1(FA_L), .I2(MUL_L), .I3(DIV_L), .I4(BSL_L), .I5(BSL_L), .I6(AND), .I7(OR), .I8(XOR),
    .I9(NOT), .I10(A), .I11({16{1'b0}}), .I12({16{1'b0}}), .I13({16{1'b0}}), .I14(SLT), .I15(SEQ), .S(S),
    .Y(YL));

  // Other names for the same wires on the sheet: BSR_H[15:0] = BSL_H; BSR_L[15:0] = BSL_L

  // Notes on the sheet:
  //   WRK: WORKING
  //   INIT: init for div circuit, must be high before (or at) first clock
  //   Output is always B {op} A
  //   Ex: B ADD A, B >> A, etc.
  //   ADD
  //   SUB
  //   MUL
  //   DIV
  //   BSR
  //   BSL
  //   AND
  //   OR
  //   XOR
  //   NOT
  //   A_PASS (MOV)
  //   ADDI
  //   SUBI
  //   MULTI
  //   SLT
  //   SEQ
endmodule
