// Digital circuit COUNT-16.dig as structural Verilog
module COUNT_16 (
  input  EN,
  input  INC,
  input  CLR,
  output [15:0] Y
);

  wire and_1_out, not_1_out;

  not not_1 (not_1_out, INC);
  and and_1 (and_1_out, EN, not_1_out);
  JK_CLR jk_clr_1 (.J(1'b1), .K(1'b1), .CLK(and_1_out), .PRE(CLR), .CLR(1'b0), .Q_2(Y[0]));  // open: Q
  JK_CLR jk_clr_2 (.J(1'b1), .K(1'b1), .CLK(Y[0]), .PRE(CLR), .CLR(1'b0), .Q_2(Y[1]));  // open: Q
  JK_CLR jk_clr_3 (.J(1'b1), .K(1'b1), .CLK(Y[1]), .PRE(CLR), .CLR(1'b0), .Q_2(Y[2]));  // open: Q
  JK_CLR jk_clr_4 (.J(1'b1), .K(1'b1), .CLK(Y[2]), .PRE(CLR), .CLR(1'b0), .Q_2(Y[3]));  // open: Q
  JK_CLR jk_clr_5 (.J(1'b1), .K(1'b1), .CLK(Y[3]), .PRE(CLR), .CLR(1'b0), .Q_2(Y[4]));  // open: Q
  JK_CLR jk_clr_6 (.J(1'b1), .K(1'b1), .CLK(Y[4]), .PRE(CLR), .CLR(1'b0), .Q_2(Y[5]));  // open: Q
  JK_CLR jk_clr_7 (.J(1'b1), .K(1'b1), .CLK(Y[5]), .PRE(CLR), .CLR(1'b0), .Q_2(Y[6]));  // open: Q
  JK_CLR jk_clr_8 (.J(1'b1), .K(1'b1), .CLK(Y[6]), .PRE(CLR), .CLR(1'b0), .Q_2(Y[7]));  // open: Q
  JK_CLR jk_clr_9 (.J(1'b1), .K(1'b1), .CLK(Y[7]), .PRE(CLR), .CLR(1'b0), .Q_2(Y[8]));  // open: Q
  JK_CLR jk_clr_10 (.J(1'b1), .K(1'b1), .CLK(Y[8]), .PRE(CLR), .CLR(1'b0), .Q_2(Y[9]));  // open: Q
  JK_CLR jk_clr_11 (.J(1'b1), .K(1'b1), .CLK(Y[9]), .PRE(CLR), .CLR(1'b0), .Q_2(Y[10]));  // open: Q
  JK_CLR jk_clr_12 (.J(1'b1), .K(1'b1), .CLK(Y[10]), .PRE(CLR), .CLR(1'b0), .Q_2(Y[11]));  // open: Q
  JK_CLR jk_clr_13 (.J(1'b1), .K(1'b1), .CLK(Y[11]), .PRE(CLR), .CLR(1'b0), .Q_2(Y[12]));  // open: Q
  JK_CLR jk_clr_14 (.J(1'b1), .K(1'b1), .CLK(Y[12]), .PRE(CLR), .CLR(1'b0), .Q_2(Y[13]));  // open: Q
  JK_CLR jk_clr_15 (.J(1'b1), .K(1'b1), .CLK(Y[13]), .PRE(CLR), .CLR(1'b0), .Q_2(Y[14]));  // open: Q
  JK_CLR jk_clr_16 (.J(1'b1), .K(1'b1), .CLK(Y[14]), .PRE(CLR), .CLR(1'b0), .Q_2(Y[15]));  // open: Q

  // Notes on the sheet:
  //   bug: increments on toggle of EN
endmodule
