// Digital circuit CPU.dig as structural Verilog
module CPU (
  input  [15:0] in_19,
  input  [7:0] in_25,
  input  INSTR_TEST,
  input  [23:0] in_27,
  input  [15:0] ADDR_PEAK,
  input  clk_2,
  input  PEEK,
  input  CLK_3,
  input  [15:0] PC_BRK,
  input  STEP,
  input  RUN,
  input  STOP,
  input  [15:0] RUNTIME_BRK,
  input  FAST__SLOW,
  input  clk_4,
  output [15:0] ZERO,
  output [15:0] out_2,
  output [15:0] out_3,
  output [15:0] KB,
  output [15:0] SP,
  output [15:0] PC,
  output [15:0] LR,
  output [15:0] BUFF,
  output [15:0] CLK,
  output [15:0] HI,
  output [15:0] G1,
  output [15:0] G2,
  output [15:0] G3,
  output [15:0] G0,
  output [15:0] G5,
  output [15:0] G6,
  output [15:0] G7,
  output [15:0] G4,
  output [31:0] out_20,
  output [15:0] out_21,
  output [15:0] out_22,
  output [3:0] out_23,
  output [15:0] out_24,
  output [31:0] out_28,
  output [15:0] ADDR,
  output [15:0] Q,
  output [31:0] out_32,
  output [15:0] D,
  output [15:0] CURRENT_PC,
  output [15:0] LAST_PC,
  output [15:0] RUNTIME,
  output STOPPED
);

  wire and_1_out, and_2_out, BNE, BRANCH, d_ff_1_q, INIT, JAL, jmp_im_sel_1_y, jmp_sel_1_y, JR, KB_CLK, KW_W,
       LD, LD_R, LD_V, LOAD, MOV, mux_1_1_y, mux_1_2_y, mux_1_4_y, not_2_out, not_3_out, or_1_out, or_2_out,
       or_4_out, or_5_out, READ_A, READ_B, STORE, STR_R, STR_V, WRITE_PC, WRITE_W, WRK, YH_WRITE;
  wire [3:0] mux_4_1_y, mux_4_2_y, mux_4_3_y, mux_4_4_y, mux_4_5_y, mux_4_6_y, mux_4_7_y;
  wire [15:0] A_EN, B_EN, driver_2_out, driverinvsel_2_out, fa_16_1_sum, inc_16_1_y, KB_IN, keyboard_1_d,
       mux_16_1_y, mux_16_2_y, mux_16_3_y, mux_16_4_y, mux_16_6_y, not_1_out, PC_IN, W;
  wire [15:15] CLK_16;

  OP_DEC op_dec_1 (.S(out_20[31:24]), .OP(out_23));
  W_SEL w_sel_1 (.S(out_20[31:24]), .Y(WRITE_W));
  B_SEL b_sel_1 (.S(out_20[31:24]), .Y(READ_B));
  A_SEL a_sel_1 (.S(out_20[31:24]), .Y(READ_A));
  STORE_SEL store_sel_1 (.S(out_20[31:24]), .Y(STORE));
  LOAD_SEL load_sel_1 (.S(out_20[31:24]), .PK(PEEK), .Y(LOAD));
  EEPROMDualPort #(.AddrBits(16), .isProgramMemory("true"), .Bits(32)) PROM (
    .A(CURRENT_PC), .Din({32{1'b0}}), .str(1'b0), .C(CLK_16[15]), .ld(1'b1), .D(out_28));
  MUX_32 mux_32_1 (.A(out_28), .B({in_25, in_27}), .A__B(INSTR_TEST), .Y(out_20));
  BRANCH_SEL branch_sel_1 (.S(out_20[31:24]), .Y(BRANCH));
  BNE_SEL bne_sel_1 (.S(out_20[31:24]), .Y(BNE));
  JR_SEL jr_sel_1 (.S(out_20[31:24]), .Y(JR));
  JAL_SEL jal_sel_1 (.S(out_20[31:24]), .Y(JAL));
  MOV_SEL mov_sel_1 (.S(out_20[31:24]), .Y(MOV));
  YL_WRITE_SEL yl_write_sel_1 (.S(out_20[31:24]), .Y(YH_WRITE));
  MUX_16 mux_16_1 (.A(out_20[15:0]), .B(out_20[19:4]), .A__B(MOV), .Y(mux_16_1_y));
  MUX_16 mux_16_2 (.A(mux_16_1_y), .B(out_22), .A__B(READ_A), .Y(mux_16_2_y));
  and and_1 (and_1_out, WRITE_W, ~WRITE_PC, ~BRANCH);  // And
  assign not_1_out = ~D;  // Not not_1, 16 bits wide
  MUX_16 mux_16_3 (.A(in_19), .B(out_21), .A__B(READ_B), .Y(mux_16_3_y));
  INC_16 inc_16_1 (.A(mux_16_2_y), .INC(JAL), .Y(inc_16_1_y));  // open: CRY
  D_FF d_ff_1 (.D(~WRK), .C(~CLK_16[15]), .Q(d_ff_1_q));  // open: nQ
  MUX_4 mux_4_1 (.A(4'b0000), .B(out_20[15:12]), .A__B(READ_A), .Y(mux_4_1_y));
  or or_1 (or_1_out, BRANCH, STORE);
  MUX_1 mux_1_1 (.A(D[0]), .B(not_1_out[0]), .A__B(BNE), .Y(mux_1_1_y));
  MUX_4 mux_4_2 (.A(4'b0000), .B(out_20[23:20]), .A__B(and_1_out), .Y(mux_4_2_y));
  MUX_4 mux_4_3 (.A(4'b0000), .B(out_20[19:16]), .A__B(READ_B), .Y(mux_4_3_y));
  or or_2 (or_2_out, BRANCH, JR, STORE);
  JMP_IM_SEL jmp_im_sel_1 (.S(out_20[31:24]), .Y(jmp_im_sel_1_y));
  JMP_SEL jmp_sel_1 (.S(out_20[31:24]), .Y(jmp_sel_1_y));
  and and_2 (and_2_out, mux_1_1_y, BRANCH);
  ALU alu_1 (
    .B(mux_16_3_y), .A(inc_16_1_y), .CIN(1'b0), .CLK(CLK_16[15]), .INIT(d_ff_1_q), .S(out_23), .YH(out_3),
    .YL(out_2), .WRK(WRK));
  MUX_4 mux_4_4 (.A(mux_4_1_y), .B(out_20[19:16]), .A__B(or_1_out), .Y(mux_4_4_y));
  MUX_16 mux_16_4 (.A(out_21), .B(out_20[23:8]), .A__B(jmp_im_sel_1_y), .Y(mux_16_4_y));
  MUX_4 mux_4_5 (.A(mux_4_2_y), .B(out_20[7:4]), .A__B(JAL), .Y(mux_4_5_y));
  MUX_4 mux_4_6 (.A(mux_4_3_y), .B(out_20[23:20]), .A__B(or_2_out), .Y(mux_4_6_y));
  MUX_4 mux_4_7 (.A(mux_4_4_y), .B(4'b0011), .A__B(JAL), .Y(mux_4_7_y));
  or or_3 (WRITE_PC, jmp_sel_1_y, and_2_out);
  assign D = ~or_4_out ? out_2 : 16'bz;  // DriverInvSel driverinvsel_1
  // DEC_4C dec_4c_1: pin names not known; wires that end beside it: mux_4_5_y, 1'b1, W
  // DEC_4C dec_4c_2: pin names not known; wires that end beside it: mux_4_6_y, 1'b1, B_EN
  // DEC_4C dec_4c_3: pin names not known; wires that end beside it: mux_4_7_y, 1'b1, A_EN
  MUX_16 mux_16_5 (.A(mux_16_4_y), .B(out_20[15:0]), .A__B(BRANCH), .Y(PC_IN));
  or or_4 (or_4_out, LOAD, STORE);
  MUX_16 mux_16_6 (.A(KB_IN), .B(out_3), .A__B(W[2]), .Y(mux_16_6_y));
  MUX_1 mux_1_2 (.A(KB_CLK), .B(CLK_16[15]), .A__B(W[2]), .Y(mux_1_2_y));
  MUX_1 mux_1_3 (.A(1'b1), .B(W[2]), .A__B(W[2]), .Y(KW_W));
  not not_2 (not_2_out, WRK);
  ZER0_16 zer0_16_1 (.B(out_21), .A(out_22), .Q(ZERO), .EN(1'b1), .B_EN(B_EN[0]), .A_EN(A_EN[0]));
  REG_16 reg_16_1 (
    .D(out_3), .CLK(CLK_16[15]), .W(YH_WRITE), .B_EN(B_EN[1]), .A_EN(A_EN[1]), .CLR(1'b0), .SET(1'b0),
    .B(out_21), .A(out_22), .Q(HI));
  REG_16 reg_16_2 (
    .D(mux_16_6_y), .CLK(mux_1_2_y), .W(KW_W), .B_EN(B_EN[2]), .A_EN(A_EN[2]), .CLR(1'b0), .SET(1'b0),
    .B(out_21), .A(out_22), .Q(KB));
  PC_16 pc_16_1 (
    .D(PC_IN), .CLK(CLK_16[15]), .W(WRITE_PC), .B_EN(B_EN[3]), .A_EN(A_EN[3]), .CLR(1'b0), .SET(1'b0),
    .INC(not_2_out), .B(out_21), .A(out_22), .Q(CURRENT_PC));
  FA_16 fa_16_1 (.A(out_20[15:0]), .B(out_21), .CIN(1'b0), .SUM(fa_16_1_sum));  // open: CRY
  BANK_SEL bank_sel_1 (.S(ADDR[15]), .EN(STORE), .VRAM(STR_V), .GEN(STR_R));
  BANK_SEL bank_sel_2 (.S(ADDR[15]), .EN(LD), .VRAM(LD_V), .GEN(LD_R));
  REG_16 reg_16_3 (
    .D(D), .CLK(CLK_16[15]), .W(W[4]), .B_EN(B_EN[4]), .A_EN(A_EN[4]), .CLR(1'b0), .SET(1'b0), .B(out_21),
    .A(out_22), .Q(SP));
  REG_16 reg_16_4 (
    .D(D), .CLK(CLK_16[15]), .W(W[5]), .B_EN(B_EN[5]), .A_EN(A_EN[5]), .CLR(1'b0), .SET(1'b0), .B(out_21),
    .A(out_22), .Q(LR));
  REG_16 reg_16_5 (
    .D(D), .CLK(CLK_16[15]), .W(W[6]), .B_EN(B_EN[6]), .A_EN(A_EN[6]), .CLR(1'b0), .SET(1'b0), .B(out_21),
    .A(out_22), .Q(BUFF));
  PC_16 pc_16_2 (
    .D(D), .CLK(CLK_16[15]), .W(W[7]), .B_EN(B_EN[7]), .A_EN(A_EN[7]), .CLR(1'b0), .SET(1'b0), .INC(1'b1),
    .B(out_21), .A(out_22), .Q(CLK));
  MUX_16 mux_16_7 (.A(fa_16_1_sum), .B(ADDR_PEAK), .A__B(PEEK), .Y(ADDR));
  assign Q = STORE ? out_22 : 16'bz;  // Driver driver_1
  and and_3 (LD, LOAD, ~STORE);  // And
  assign driver_2_out = ADDR[15] ? ADDR : 16'bz;  // Driver driver_2
  assign driverinvsel_2_out = ~ADDR[15] ? ADDR : 16'bz;  // DriverInvSel driverinvsel_2
  REG_16 reg_16_6 (
    .D(D), .CLK(CLK_16[15]), .W(W[8]), .B_EN(B_EN[8]), .A_EN(A_EN[8]), .CLR(1'b0), .SET(1'b0), .B(out_21),
    .A(out_22), .Q(G0));
  REG_16 reg_16_7 (
    .D(D), .CLK(CLK_16[15]), .W(W[9]), .B_EN(B_EN[9]), .A_EN(A_EN[9]), .CLR(1'b0), .SET(1'b0), .B(out_21),
    .A(out_22), .Q(G1));
  REG_16 reg_16_8 (
    .D(D), .CLK(CLK_16[15]), .W(W[10]), .B_EN(B_EN[10]), .A_EN(A_EN[10]), .CLR(1'b0), .SET(1'b0), .B(out_21),
    .A(out_22), .Q(G2));
  REG_16 reg_16_9 (
    .D(D), .CLK(CLK_16[15]), .W(W[11]), .B_EN(B_EN[11]), .A_EN(A_EN[11]), .CLR(1'b0), .SET(1'b0), .B(out_21),
    .A(out_22), .Q(G3));
  Keyboard keyboard_1 (.C(KB_CLK), .en(1'b1), .D(keyboard_1_d), .av(KB_CLK));
  GraphicCard #(.graphicHeight(19), .graphicWidth(16), .Bits(16)) graphiccard_1 (
    .A(driver_2_out[9:0]), .str(STR_V), .C(CLK_16[15]), .ld(LD_V), .B(1'b0), .D(Q));
  RAMSinglePort #(.AddrBits(13), .Bits(16)) RAM (
    .A(driverinvsel_2_out[12:0]), .str(STR_R), .C(CLK_16[15]), .ld(LD_R), .D(Q));
  D_FF #(.Bits(16)) d_ff_2 (.D(keyboard_1_d), .C(KB_CLK), .Q(KB_IN));  // open: nQ
  assign D = LD ? Q : 16'bz;  // Driver driver_3
  REG_16 reg_16_10 (
    .D(D), .CLK(CLK_16[15]), .W(W[12]), .B_EN(B_EN[12]), .A_EN(A_EN[12]), .CLR(1'b0), .SET(1'b0), .B(out_21),
    .A(out_22), .Q(G4));
  REG_16 reg_16_11 (
    .D(D), .CLK(CLK_16[15]), .W(W[13]), .B_EN(B_EN[13]), .A_EN(A_EN[13]), .CLR(1'b0), .SET(1'b0), .B(out_21),
    .A(out_22), .Q(G5));
  REG_16 reg_16_12 (
    .D(D), .CLK(CLK_16[15]), .W(W[14]), .B_EN(B_EN[14]), .A_EN(A_EN[14]), .CLR(1'b0), .SET(1'b0), .B(out_21),
    .A(out_22), .Q(G6));
  REG_16 reg_16_13 (
    .D(D), .CLK(CLK_16[15]), .W(W[15]), .B_EN(B_EN[15]), .A_EN(A_EN[15]), .CLR(1'b0), .SET(1'b0), .B(out_21),
    .A(out_22), .Q(G7));
  INIT init_1 (.A(CLK_16[15]), .Y(INIT));
  MUX_1 mux_1_4 (.A(clk_2), .B(clk_4), .A__B(FAST__SLOW), .Y(mux_1_4_y));
  BRK_SEL brk_sel_1 (
    .PC(CURRENT_PC), .BRK_P(PC_BRK), .RUNTIME(RUNTIME), .BRK_R(RUNTIME_BRK), .STEP(STEP), .RUN(RUN),
    .Y(STOPPED));
  MUX_1 mux_1_5 (.A(mux_1_4_y), .B(CLK_3), .A__B(or_5_out), .Y(CLK_16[15]));
  or or_5 (or_5_out, STOP, STOPPED);
  not not_3 (not_3_out, CLK_16[15]);
  LAST_PC last_pc_1 (.PC_IN(CURRENT_PC), .CLK(CLK_16[15]), .PC_OUT(LAST_PC));
  COUNT_16 count_16_1 (.SET(1'b0), .CLK(not_3_out), .CLR(INIT), .Y(RUNTIME));

  assign out_24 = D;
  assign out_32 = out_20;
  assign PC = CURRENT_PC;

  // Other names for the same wires on the sheet: A_OUT[15:0] = out_22; VRAM__RAM = ADDR[15]; B_OUT[15:0] = out_21;
  //   CLK_16[14:0] = {15{CLK_16[15]}}; CLK_t = CLK_16[15]; D_t[15:0] = Q; _0_15[15:0] = out_20[15:0];
  //   INSTR[31:0] = out_20; _4_7[3:0] = out_20[7:4]; _4_19[15:0] = out_20[19:4]; _8_23[15:0] = out_20[23:8];
  //   _12_15[3:0] = out_20[15:12]; _16_19[3:0] = out_20[19:16]; _20_23[3:0] = out_20[23:20];
  //   _24_31[7:0] = out_20[31:24]; OP[3:0] = out_23; STR = STORE; W_2 = W[2]; YH[15:0] = out_3; YL[15:0] = D

  // Notes on the sheet:
  //   clk_2: Hz: 1000
  //   PC_BRK: default -1
  //   RUN: default 1
  //   RUNTIME_BRK: default -1
  //   clk_4: Hz: 50
  //   contents of PROM (hex, n*v repeats v):
  //   302e3276,4646460a,41410a46,410a4141,a414141,46464646
  //   ADDR < 0x8000 ->  RAM
  //   ADDR >= 0x8000 -> VRAM1
  //   ADDR >= 0x8100 -> VRAM2
  //   contents of PROM (hex, n*v repeats v):
  //   C:\Users\Chris\Documents\VS Code\asm\program.hex false
endmodule
