// Digital circuit TEMP.dig as structural Verilog
module TEMP (
  input  B1,
  input  A1,
  input  B0,
  input  A0,
  input  Cin,
  input  B2,
  input  A2,
  input  B3,
  input  A3,
  input  J,
  input  K,
  input  CLK,
  input  A,
  input  B,
  input  C,
  output out_10,
  output out_11,
  output out_12,
  output out_13,
  output out_14,
  output Q,
  output Q_2,
  output Z
);

  wire and_1_out, and_2_out, and_3_out, and_4_out, and_5_out, and_6_out, and_7_out, and_8_out, and_9_out,
       nand_1_out, nand_2_out, not_1_out, or_3_out, or_4_out, or_5_out, xor_1_out, xor_2_out, xor_3_out,
       xor_4_out;

  nand nand_1 (nand_1_out, Q_2, J, CLK);
  nand nand_2 (nand_2_out, CLK, K, Q);
  and and_1 (and_1_out, A, B);
  nand nand_3 (Q, nand_1_out, Q_2);
  nand nand_4 (Q_2, Q, nand_2_out);
  not not_1 (not_1_out, and_1_out);
  or or_1 (Z, not_1_out, C);
  xor xor_1 (xor_1_out, B3, A3);
  and and_2 (and_2_out, A3, B3);
  xor xor_2 (xor_2_out, B2, A2);
  and and_3 (and_3_out, A2, B2);
  xor xor_3 (xor_3_out, B1, A1);
  and and_4 (and_4_out, A1, B1);
  xor xor_4 (xor_4_out, B0, A0);
  and and_5 (and_5_out, A0, B0);
  xor xor_5 (out_11, xor_1_out, or_3_out);
  and and_6 (and_6_out, or_3_out, xor_1_out);
  xor xor_6 (out_12, xor_2_out, or_4_out);
  and and_7 (and_7_out, or_4_out, xor_2_out);
  xor xor_7 (out_13, xor_3_out, or_5_out);
  and and_8 (and_8_out, or_5_out, xor_3_out);
  xor xor_8 (out_14, xor_4_out, Cin);
  and and_9 (and_9_out, Cin, xor_4_out);
  or or_2 (out_10, and_6_out, and_2_out);
  or or_3 (or_3_out, and_7_out, and_3_out);
  or or_4 (or_4_out, and_8_out, and_4_out);
  or or_5 (or_5_out, and_9_out, and_5_out);

  // Notes on the sheet:
  //   MIDDLE
endmodule
