// Digital circuit YL_WRITE_SEL.dig as structural Verilog
module YL_WRITE_SEL (
  input  [7:0] S,
  output Y
);

  wire and_1_out, and_2_out, not_1_out, not_2_out, not_3_out, not_4_out;

  not not_1 (not_1_out, S[4]);
  not not_2 (not_2_out, S[3]);
  not not_3 (not_3_out, S[2]);
  not not_4 (not_4_out, S[1]);
  and and_1 (and_1_out, not_1_out, not_2_out, not_3_out, S[1]);
  and and_2 (and_2_out, not_1_out, not_2_out, S[2], not_4_out);
  or or_1 (Y, and_1_out, and_2_out);
endmodule
